// Digital circuit 4BIT_CPU_Circuit.dig as structural Verilog
module _4BIT_CPU_Circuit (
  input  Clock,
  input  LoadAddress,
  input  [3:0] Address_Jump,
  output [3:0] out_2,
  output [3:0] out_4
);

  wire _4bit_fulladdersubtractor_1_carry, not_1_out, not_2_out;
  wire [3:0] _4bit_fulladdersubtractor_1_sum, multiplexer_1_out, RAM_16__4_d;

  _4bit_fullAdderSubtractor _4bit_fulladdersubtractor_1 (
    .A(out_2), .B(4'b0001), .C_in(1'b0), .Sum(_4bit_fulladdersubtractor_1_sum),
    .Carry(_4bit_fulladdersubtractor_1_carry));
  not not_1 (not_1_out, Clock);
  Multiplexer #(.Bits(4)) multiplexer_1 (
    .sel(LoadAddress), .in_0(_4bit_fulladdersubtractor_1_sum), .in_1(Address_Jump), .out(multiplexer_1_out));
  Register #(.Bits(4)) PC (.D(multiplexer_1_out), .C(not_1_out), .en(not_1_out), .Q(out_2));
  BlockRAMDualPort #(.AddrBits(4), .Bits(4)) RAM_16__4 (
    .A(out_2), .Din(4'b0110), .str(Clock), .C(Clock), .D(RAM_16__4_d));
  not not_2 (not_2_out, Clock);
  Register #(.Bits(4)) IR (.D(RAM_16__4_d), .C(not_2_out), .en(not_2_out), .Q(out_4));
  // also tied to GND on the sheet: _4bit_fulladdersubtractor_1_carry
endmodule
