// Digital circuit ControlUnit.dig as structural Verilog
module ControlUnit (
  input  A,
  input  B,
  input  C,
  input  D,
  output WR,
  output WE,
  output IL,
  output ADD,
  output SUB,
  output AND,
  output OR,
  output XOR,
  output RR_2,
  output RR_1,
  output SLT
);

  wire and_4_out, and_5_out, and_6_out, and_7_out, not_2_out, not_3_out, not_4_out;

  and and_1 (SLT, A, B, C, not_3_out);
  and and_2 (OR, A, B, not_4_out, not_3_out);
  and and_3 (AND, A, not_2_out, C, D);
  not not_1 (RR_1, A);
  not not_2 (not_2_out, B);
  not not_3 (not_3_out, D);
  not not_4 (not_4_out, C);
  and and_4 (and_4_out, RR_1, not_2_out, C);
  and and_5 (and_5_out, A, not_4_out, not_3_out);
  and and_6 (and_6_out, RR_1, C);
  and and_7 (and_7_out, RR_1, D);
  or or_1 (WR, and_4_out, and_5_out);
  or or_2 (IL, and_6_out, and_7_out);
  or or_3 (WE, A, C, D);
  and and_8 (XOR, A, B, not_4_out, D);
  and and_9 (ADD, A, not_2_out, not_4_out, D);
  and and_10 (SUB, A, not_2_out, C, not_3_out);

  assign RR_2 = 1'b1;
endmodule
